// Digital circuit add and compare.dig as structural Verilog
module add_and_compare (
  input  [7:0] A,
  input  [7:0] B,
  input  Cin,
  output [7:0] S,
  output C,
  output O,
  output Z
);

  wire add_2_c_o;

  Add add_1 (.a(A[0]), .b(B[0]), .c_i(add_2_c_o), .s(S[0]), .c_o(C));
  Add #(.Bits(7)) add_2 (.a(A[7:1]), .b(B[7:1]), .c_i(Cin), .s(S[7:1]), .c_o(add_2_c_o));
  xor xor_1 (O, C, add_2_c_o);
  nor nor_1 (Z, S[0], S[1], S[2], S[3], S[4], S[5], S[6], S[7]);
endmodule
