// Digital circuit adder with overflow.dig as structural Verilog
module adder_with_overflow (
  input  [7:0] A,
  input  [7:0] B,
  input  Cin,
  output [7:0] S,
  output C,
  output O
);

  Add add_1 (.a(A[0]), .b(B[0]), .c_i(S[1]), .s(S[0]), .c_o(C));
  Add #(.Bits(7)) add_2 (.a(A[7:1]), .b(B[7:1]), .c_i(Cin), .c_o(S[1]));  // open: s
  xor xor_1 (O, C, S[1]);
  // Pins of 1 and 7 bits meet at S[7:1]
endmodule
