// Digital circuit antikythera.dig as structural Verilog
module antikythera (
);

  wire A_Enable, ALU_A_Enable, ALU_B_Enable, ALU_CF_Enable, ALU_Cin_Override, ALU_Invert, and_2_out,
       AR_Enable, B_Enable, CF, comparator_1_eq, demultiplexer_1_out_0, demultiplexer_1_out_1,
       demultiplexer_1_out_2, demultiplexer_1_out_3, FR_Enable, IP_Enable, IP_Load, Memory_Load,
       Memory_Store, not_1_out, OF, or_1_out, or_2_out, or_3_out, or_4_out, or_6_out, RR_Enable, SF,
       ST2_Select, TR_Enable, undriven, undriven_3, undriven_4, undriven_5, ZF;
  wire [1:0] ALU_A_In_Select, ALU_B_In_Select, ALU_Select, Mem_IN_Select, TR_In_Select;
  wire [3:1] add_and_compare_1_c;
  wire [7:0] A_q, add_and_compare_1_s, ALU_A_q, ALU_B_q, and_1_out, AR_q, c__addr_q, demultiplexer_2_out_0,
       demultiplexer_2_out_1, demultiplexer_2_out_2, demultiplexer_2_out_3, IP_out, IR0_q, IR1_q, IR2_q,
       lower_d, multiplexer_1_out, multiplexer_2_out, multiplexer_3_out, multiplexer_4_out,
       multiplexer_5_out, multiplexer_6_out, multiplexer_7_out, multiplexer_8_out, multiplexer_9_out,
       multiplexer_10_out, multiplexer_11_out, multiplexer_12_out, multiplexer_13_out, multiplexer_14_out,
       multiplexer_15_out, multiplexer_16_out, or_5_out, ramdualport_1_d, ramdualport_2_d, ramdualport_3_d,
       ramdualport_4_d, register_1_q, register_2_q, register_3_q, register_4_q, rom_1_d, rom_1_d_2,
       rom_1_d_3, rom_1_d_4, RR_q, TR_q, undriven_6, upper_d, X_q, xor_1_out, xor_2_out;
  wire [7:1] undriven_2;

  Multiplexer #(.Selector_Bits(2), .Bits(8)) multiplexer_1 (
    .in_0(register_4_q), .in_1(register_3_q), .in_2(register_2_q), .in_3(register_1_q),
    .out(multiplexer_1_out));  // open: sel
  Register #(.Bits(8)) c__addr (.D(undriven_6), .Q(c__addr_q));  // open: C, en
  RAMDualPort #(.Bits(8)) ramdualport_1 (
    .A(undriven_6[5:4]), .Din(register_4_q), .str(1'b0), .C(1'b0), .ld(1'b0), .D(ramdualport_1_d));
  RAMDualPort #(.Bits(8)) ramdualport_2 (
    .A(undriven_6[5:4]), .Din(register_3_q), .str(1'b0), .C(1'b0), .ld(1'b0), .D(ramdualport_2_d));
  RAMDualPort #(.Bits(8)) ramdualport_3 (
    .A(undriven_6[5:4]), .Din(register_2_q), .str(1'b0), .C(1'b0), .ld(1'b0), .D(ramdualport_3_d));
  RAMDualPort #(.Bits(8)) ramdualport_4 (
    .A(undriven_6[5:4]), .Din(register_1_q), .str(1'b0), .C(1'b0), .ld(1'b0), .D(ramdualport_4_d));
  ROM #(.AddrBits(5), .Bits(32)) rom_1 (
    .A(undriven_6[5:1]), .sel(1'b1), .D({rom_1_d_4, rom_1_d_3, rom_1_d_2, rom_1_d}));
  Comparator #(.Bits(8)) comparator_1 (.a(c__addr_q), .b(undriven_6), .eq(comparator_1_eq));  // open: gt, lt
  Register #(.Bits(8)) register_1 (.D(multiplexer_2_out), .C(undriven_5), .en(or_1_out), .Q(register_1_q));
  Register #(.Bits(8)) register_2 (.D(multiplexer_3_out), .C(undriven_5), .en(or_2_out), .Q(register_2_q));
  Register #(.Bits(8)) register_3 (.D(multiplexer_4_out), .C(undriven_5), .en(or_3_out), .Q(register_3_q));
  Register #(.Bits(8)) register_4 (.D(multiplexer_5_out), .C(undriven_5), .en(or_4_out), .Q(register_4_q));
  Multiplexer #(.Bits(8)) multiplexer_2 (
    .sel(undriven_4), .in_0(demultiplexer_2_out_3), .in_1(multiplexer_9_out), .out(multiplexer_2_out));
  Multiplexer #(.Bits(8)) multiplexer_3 (
    .sel(undriven_4), .in_0(demultiplexer_2_out_2), .in_1(multiplexer_8_out), .out(multiplexer_3_out));
  Multiplexer #(.Bits(8)) multiplexer_4 (
    .sel(undriven_4), .in_0(demultiplexer_2_out_1), .in_1(multiplexer_7_out), .out(multiplexer_4_out));
  Multiplexer #(.Bits(8)) multiplexer_5 (
    .sel(undriven_4), .in_0(demultiplexer_2_out_0), .in_1(multiplexer_6_out), .out(multiplexer_5_out));
  Multiplexer #(.Bits(8)) multiplexer_6 (
    .sel(undriven_6[0]), .in_0(ramdualport_1_d), .in_1(rom_1_d), .out(multiplexer_6_out));
  Multiplexer #(.Bits(8)) multiplexer_7 (
    .sel(undriven_6[0]), .in_0(ramdualport_2_d), .in_1(rom_1_d_2), .out(multiplexer_7_out));
  Multiplexer #(.Bits(8)) multiplexer_8 (
    .sel(undriven_6[0]), .in_0(ramdualport_3_d), .in_1(rom_1_d_3), .out(multiplexer_8_out));
  Multiplexer #(.Bits(8)) multiplexer_9 (
    .sel(undriven_6[0]), .in_0(ramdualport_4_d), .in_1(rom_1_d_4), .out(multiplexer_9_out));
  or or_1 (or_1_out, demultiplexer_1_out_3, undriven_3);
  or or_2 (or_2_out, demultiplexer_1_out_2, undriven_3);
  or or_3 (or_3_out, demultiplexer_1_out_1, undriven_3);
  or or_4 (or_4_out, demultiplexer_1_out_0, undriven_3);
  Demultiplexer #(.Selector_Bits(2)) demultiplexer_1 (
    .in(1'b0), .out_0(demultiplexer_1_out_0), .out_1(demultiplexer_1_out_1), .out_2(demultiplexer_1_out_2),
    .out_3(demultiplexer_1_out_3));  // open: sel
  Demultiplexer #(.Selector_Bits(2)) demultiplexer_2 (
    .in(1'b0), .out_0(demultiplexer_2_out_0[0]), .out_1(demultiplexer_2_out_1[0]),
    .out_2(demultiplexer_2_out_2[0]), .out_3(demultiplexer_2_out_3[0]));  // open: sel
  CounterPreset #(.Bits(8)) IP (
    .en(IP_Enable), .C(undriven), .dir(1'b0), .in(multiplexer_16_out), .ld(IP_Load), .clr(1'b0), .out(IP_out));  // open: ovf
  Register #(.Bits(8)) RR (.D(IP_out), .C(undriven), .en(RR_Enable), .Q(RR_q));
  Register #(.Bits(8)) AR (.D(multiplexer_14_out), .C(undriven), .en(AR_Enable), .Q(AR_q));
  Register #(.Bits(8)) IR0 (.D(multiplexer_14_out), .C(undriven), .en(1'b1), .Q(IR0_q));
  Multiplexer #(.Selector_Bits(2), .Bits(8)) multiplexer_10 (
    .sel(TR_In_Select), .in_0(A_q), .in_1(X_q), .in_2(RR_q), .in_3(multiplexer_14_out),
    .out(multiplexer_10_out));
  Multiplexer #(.Selector_Bits(2), .Bits(8)) multiplexer_11 (
    .sel(ALU_A_In_Select), .in_0(A_q), .in_1(X_q), .in_2(IP_out), .in_3(multiplexer_14_out),
    .out(multiplexer_11_out));
  Multiplexer #(.Selector_Bits(2), .Bits(8)) multiplexer_12 (
    .sel(ALU_B_In_Select), .in_0(A_q), .in_1(X_q), .in_2({undriven_2, 1'b0}), .in_3(multiplexer_14_out),
    .out(multiplexer_12_out));
  Multiplexer #(.Selector_Bits(2), .Bits(8)) multiplexer_13 (
    .sel(Mem_IN_Select), .in_0(A_q), .in_1(X_q), .in_2(IP_out), .in_3(AR_q), .out(multiplexer_13_out));
  Register #(.Bits(8)) IR1 (.D(IR0_q), .C(undriven), .en(1'b1), .Q(IR1_q));
  Register #(.Bits(8)) IR2 (.D(IR1_q), .C(undriven), .en(1'b1), .Q(IR2_q));
  ROM #(.AddrBits(7), .Bits(8)) upper (.A(multiplexer_13_out[7:1]), .sel(multiplexer_13_out[0]), .D(upper_d));
  not not_1 (not_1_out, multiplexer_13_out[0]);
  RAMDualPort #(.AddrBits(4), .Bits(8)) lower (
    .A(multiplexer_13_out[7:4]), .Din(multiplexer_16_out), .str(Memory_Store), .C(undriven),
    .ld(Memory_Load), .D(lower_d));
  Register #(.Bits(8)) TR (.D(multiplexer_10_out), .C(undriven), .en(TR_Enable), .Q(TR_q));
  Register #(.Bits(8)) ALU_A (.D(multiplexer_11_out), .C(undriven), .en(ALU_A_Enable), .Q(ALU_A_q));
  Register #(.Bits(8)) ALU_B (.D(multiplexer_12_out), .C(undriven), .en(ALU_B_Enable), .Q(ALU_B_q));
  Multiplexer #(.Bits(8)) multiplexer_14 (.sel(not_1_out), .in_0(upper_d), .in_1(lower_d), .out(multiplexer_14_out));
  xor xor_1 (xor_1_out[0], ALU_B_q[0], ALU_Invert);
  assign and_1_out = xor_1_out & ALU_A_q;  // And and_1, 8 bits wide
  assign or_5_out = xor_1_out | ALU_A_q;  // Or or_5, 8 bits wide
  assign xor_2_out = xor_1_out ^ ALU_A_q;  // XOr xor_2, 8 bits wide
  add_and_compare add_and_compare_1 (
    .A(ALU_A_q), .B(xor_1_out), .Cin(or_6_out), .S(add_and_compare_1_s), .C(add_and_compare_1_c[1]),
    .O(add_and_compare_1_c[2]), .Z(add_and_compare_1_c[3]));
  or or_6 (or_6_out, ALU_Cin_Override, and_2_out);
  and and_2 (and_2_out, ALU_CF_Enable, CF);
  Multiplexer #(.Selector_Bits(2), .Bits(8)) multiplexer_15 (
    .sel(ALU_Select), .in_0(and_1_out), .in_1(or_5_out), .in_2(xor_2_out), .in_3(add_and_compare_1_s),
    .out(multiplexer_15_out));
  Multiplexer #(.Bits(8)) multiplexer_16 (
    .sel(ST2_Select), .in_0(TR_q), .in_1(multiplexer_15_out), .out(multiplexer_16_out));
  Register #(.Bits(4)) FR (
    .D({add_and_compare_1_c, add_and_compare_1_s[0]}), .C(undriven), .en(FR_Enable), .Q({ZF, OF, CF, SF}));
  Register #(.Bits(8)) A (.D(multiplexer_16_out), .C(undriven), .en(A_Enable), .Q(A_q));
  Register #(.Bits(8)) X (.D(multiplexer_16_out), .C(undriven), .en(B_Enable), .Q(X_q));
  // Pins of 1 and 8 bits meet at ALU_B_q
  // Pins of 1 and 8 bits meet at {8{ALU_Invert}}
  // Pins of 1 and 8 bits meet at xor_1_out
  // Pins of 1 and 8 bits meet at demultiplexer_2_out_0
  // Pins of 1 and 8 bits meet at demultiplexer_2_out_1
  // Pins of 1 and 8 bits meet at demultiplexer_2_out_2
  // Pins of 1 and 8 bits meet at demultiplexer_2_out_3
  // Pins of 1 and 8 bits meet at {undriven_2, 1'b0}

  // Notes on the sheet:
  //   dout
  //   address
  //   cache (1)
  //   hit
  //   din
  //   ST0
  //   zero
  //   ST1
  //   ALU
  //   ST2
  //   use ST1 & result instead
  //   of ST2 & A/B if the ALU is
  //   limiting clock speed rather
  //   than memory
endmodule
