// Digital circuit memory interface.dig as structural Verilog
module memory_interface (
  input  [15:0] new_address,
  input  clk,
  input  [15:0] old_address,
  input  [7:0] data
);

  wire and_1_out, and_2_out, and_3_out, comparator_1_eq, comparator_2_eq, demultiplexer_2_out_0,
       demultiplexer_2_out_1, demultiplexer_2_out_2, demultiplexer_2_out_3, not_1_out, or_1_out, or_2_out,
       or_3_out, or_4_out, undriven_2, undriven_3, undriven_4;
  wire [1:0] d_id_out, q_in_out, q_out_out;
  wire [2:0] C0_COMMAND;
  wire [7:0] _64k_d, C0_DATA_OUT, C1_DATA_OUT, C2_DATA_OUT, C3_DATA_OUT, c__addr_q, demultiplexer_3_out_0,
       demultiplexer_3_out_1, demultiplexer_3_out_2, demultiplexer_3_out_3, multiplexer_2_out,
       multiplexer_3_out, multiplexer_6_out, multiplexer_7_out, multiplexer_8_out, multiplexer_9_out,
       multiplexer_10_out, multiplexer_11_out, multiplexer_12_out, multiplexer_13_out, ramdualport_1_d,
       ramdualport_2_d, ramdualport_3_d, ramdualport_4_d, register_1_q, register_2_q, register_3_q,
       register_4_q, rom_1_d, rom_1_d_2, rom_1_d_3, rom_1_d_4, undriven;
  wire [15:0] multiplexer_4_out, multiplexer_5_out;
  wire [17:0] queue_d2;
  wire [18:0] multiplexer_1_out;

  DipSwitch dipswitch_1 (.out(C0_COMMAND[0]));
  DipSwitch dipswitch_2 (.out(C0_COMMAND[1]));
  DipSwitch dipswitch_3 (.out(C0_COMMAND[2]));
  Counter d_id (.en(1'b1), .C(clk), .out(d_id_out[0]));  // open: clr, ovf
  Multiplexer #(.Selector_Bits(2), .Bits(19)) multiplexer_1 (
    .sel(d_id_out), .in_0({new_address, C0_COMMAND}), .in_1({new_address, C0_COMMAND}),
    .in_2({new_address, C0_COMMAND}), .in_3({new_address, C0_COMMAND}), .out(multiplexer_1_out));
  and and_1 (and_1_out, clk, multiplexer_1_out[0]);
  and and_2 (and_2_out, clk, and_3_out);
  Counter #(.Bits(2)) q_in (.en(1'b1), .C(and_1_out), .out(q_in_out));  // open: clr, ovf
  Counter #(.Bits(2)) q_out (.en(1'b1), .C(and_2_out), .out(q_out_out));  // open: clr, ovf
  RAMDualAccess #(.Bits(18)) queue (
    .str(and_1_out), .C(clk), .A1(q_in_out), .Din1(multiplexer_1_out[18:1]), .A2(q_out_out), .D2(queue_d2));  // open: ld, D1
  Comparator #(.Bits(2)) comparator_1 (.a(q_in_out), .b(q_out_out), .eq(comparator_1_eq));  // open: gt, lt
  Multiplexer #(.Selector_Bits(2), .Bits(8)) multiplexer_2 (
    .in_0(register_4_q), .in_1(register_3_q), .in_2(register_2_q), .in_3(register_1_q),
    .out(multiplexer_2_out));  // open: sel
  not not_1 (not_1_out, comparator_1_eq);
  Register #(.Bits(8)) c__addr (.D(undriven), .Q(c__addr_q));  // open: C, en
  buf and_3 (and_3_out, not_1_out);  // And open: In_1
  RAMDualPort #(.Bits(8)) ramdualport_1 (
    .A(undriven[5:4]), .Din(register_4_q), .str(1'b0), .C(1'b0), .ld(1'b0), .D(ramdualport_1_d));
  RAMDualPort #(.Bits(8)) ramdualport_2 (
    .A(undriven[5:4]), .Din(register_3_q), .str(1'b0), .C(1'b0), .ld(1'b0), .D(ramdualport_2_d));
  RAMDualPort #(.Bits(8)) ramdualport_3 (
    .A(undriven[5:4]), .Din(register_2_q), .str(1'b0), .C(1'b0), .ld(1'b0), .D(ramdualport_3_d));
  RAMDualPort #(.Bits(8)) ramdualport_4 (
    .A(undriven[5:4]), .Din(register_1_q), .str(1'b0), .C(1'b0), .ld(1'b0), .D(ramdualport_4_d));
  ROM #(.AddrBits(5), .Bits(32)) rom_1 (.A(undriven[5:1]), .sel(1'b1), .D({rom_1_d_4, rom_1_d_3, rom_1_d_2, rom_1_d}));
  Comparator #(.Bits(8)) comparator_2 (.a(c__addr_q), .b(undriven), .eq(comparator_2_eq));  // open: gt, lt
  Multiplexer #(.Selector_Bits(2), .Bits(8)) multiplexer_3 (
    .sel(queue_d2[1:0]), .in_0(data), .in_1(data), .in_2(data), .in_3(data), .out(multiplexer_3_out));
  Multiplexer #(.Selector_Bits(2), .Bits(16)) multiplexer_4 (
    .sel(queue_d2[1:0]), .in_0(old_address), .in_1(old_address), .in_2(old_address), .in_3(old_address),
    .out(multiplexer_4_out));
  Register #(.Bits(8)) register_1 (.D(multiplexer_6_out), .C(undriven_2), .en(or_1_out), .Q(register_1_q));
  Register #(.Bits(8)) register_2 (.D(multiplexer_7_out), .C(undriven_2), .en(or_2_out), .Q(register_2_q));
  Register #(.Bits(8)) register_3 (.D(multiplexer_8_out), .C(undriven_2), .en(or_3_out), .Q(register_3_q));
  Register #(.Bits(8)) register_4 (.D(multiplexer_9_out), .C(undriven_2), .en(or_4_out), .Q(register_4_q));
  Multiplexer #(.Bits(16)) multiplexer_5 (
    .in_0(multiplexer_4_out), .in_1(queue_d2[17:2]), .out(multiplexer_5_out));  // open: sel
  Multiplexer #(.Bits(8)) multiplexer_6 (
    .sel(undriven_3), .in_0(demultiplexer_3_out_3), .in_1(multiplexer_13_out), .out(multiplexer_6_out));
  Multiplexer #(.Bits(8)) multiplexer_7 (
    .sel(undriven_3), .in_0(demultiplexer_3_out_2), .in_1(multiplexer_12_out), .out(multiplexer_7_out));
  Multiplexer #(.Bits(8)) multiplexer_8 (
    .sel(undriven_3), .in_0(demultiplexer_3_out_1), .in_1(multiplexer_11_out), .out(multiplexer_8_out));
  Multiplexer #(.Bits(8)) multiplexer_9 (
    .sel(undriven_3), .in_0(demultiplexer_3_out_0), .in_1(multiplexer_10_out), .out(multiplexer_9_out));
  Multiplexer #(.Bits(8)) multiplexer_10 (
    .sel(undriven[0]), .in_0(ramdualport_1_d), .in_1(rom_1_d), .out(multiplexer_10_out));
  Multiplexer #(.Bits(8)) multiplexer_11 (
    .sel(undriven[0]), .in_0(ramdualport_2_d), .in_1(rom_1_d_2), .out(multiplexer_11_out));
  Multiplexer #(.Bits(8)) multiplexer_12 (
    .sel(undriven[0]), .in_0(ramdualport_3_d), .in_1(rom_1_d_3), .out(multiplexer_12_out));
  Multiplexer #(.Bits(8)) multiplexer_13 (
    .sel(undriven[0]), .in_0(ramdualport_4_d), .in_1(rom_1_d_4), .out(multiplexer_13_out));
  RAMDualPort #(.AddrBits(16), .Bits(8)) _64k (
    .A(multiplexer_5_out), .Din(multiplexer_3_out), .D(_64k_d));  // open: str, C, ld
  Demultiplexer #(.Selector_Bits(2), .Bits(8)) demultiplexer_1 (
    .sel(queue_d2[1:0]), .in(_64k_d), .out_0(C0_DATA_OUT), .out_1(C1_DATA_OUT), .out_2(C2_DATA_OUT),
    .out_3(C3_DATA_OUT));
  or or_1 (or_1_out, demultiplexer_2_out_3, undriven_4);
  or or_2 (or_2_out, demultiplexer_2_out_2, undriven_4);
  or or_3 (or_3_out, demultiplexer_2_out_1, undriven_4);
  or or_4 (or_4_out, demultiplexer_2_out_0, undriven_4);
  Demultiplexer #(.Selector_Bits(2)) demultiplexer_2 (
    .in(1'b0), .out_0(demultiplexer_2_out_0), .out_1(demultiplexer_2_out_1), .out_2(demultiplexer_2_out_2),
    .out_3(demultiplexer_2_out_3));  // open: sel
  Demultiplexer #(.Selector_Bits(2)) demultiplexer_3 (
    .in(1'b0), .out_0(demultiplexer_3_out_0[0]), .out_1(demultiplexer_3_out_1[0]),
    .out_2(demultiplexer_3_out_2[0]), .out_3(demultiplexer_3_out_3[0]));  // open: sel
  // Pins of 1 and 2 bits meet at d_id_out
  // Pins of 1 and 8 bits meet at demultiplexer_3_out_0
  // Pins of 1 and 8 bits meet at demultiplexer_3_out_1
  // Pins of 1 and 8 bits meet at demultiplexer_3_out_2
  // Pins of 1 and 8 bits meet at demultiplexer_3_out_3

  // Other names for the same wires on the sheet: C1_COMMAND[18:0] = {new_address, C0_COMMAND};
  //   C2_COMMAND[18:0] = {new_address, C0_COMMAND}; C3_COMMAND[18:0] = {new_address, C0_COMMAND};
  //   C0_ADDRESS[15:0] = old_address; C1_ADDRESS[15:0] = old_address; C2_ADDRESS[15:0] = old_address;
  //   C3_ADDRESS[15:0] = old_address; C0_DATA_IN[7:0] = data; C1_DATA_IN[7:0] = data; C2_DATA_IN[7:0] = data;
  //   C3_DATA_IN[7:0] = data; clock = clk; C0_COMMAND[18:3] = new_address

  // Notes on the sheet:
  //   dout
  //   address
  //   cache (1)
  //   hit
  //   din
endmodule
